# Fritzing sketch RGB led (saved by Fritzing 0.9.3b)
breadboards: 1

parts:
  LED1 = RGB LED - (4 legs) [package="5 mm [THT]"]
  U1 = NodeMCU V1.0
  R1 = Resistor [tolerance=±5% resistance=220 package=THT]
  R2 = Resistor [tolerance=±5% resistance=220 package=THT]
  R3 = Resistor [tolerance=±5% resistance=220 package=THT]

nets:
  N1: LED1.red_cathode, R1.Pin_1
  N2: LED1.common_anode, U1.GND
  N3: LED1.green_cathode, R2.Pin_1
  N4: LED1.blue_cathode, R3.Pin_1
  N5: U1.D2, R1.Pin_0
  N6: U1.D5, R2.Pin_0
  N7: U1.D6, R3.Pin_0

custom parts:
  NodeMCU V1.0: ESP8266 based NodeMCU
